// Logisim project input.circ as structural Verilog: 1 circuit, main circuit main
module main (
);

  wire Runway_Picker_p2, Runway_Picker_p3;
  wire [3:0] Runway_Picker_p1;

  // runway_picker_main Runway_Picker: pin names not known; wires that end beside it: Runway_Picker_p1, Runway_Picker_p2, Runway_Picker_p3
  runway_status_main Runway_status (
    .Runway_B_status(Runway_Picker_p3), .Runway_A_status(Runway_Picker_p2), .in_1(Runway_Picker_p1));
endmodule
